# Fritzing sketch Schema 1 (saved by Fritzing 0.9.3b)

parts:
  SIM868 = FTDI Basic Programmer
  Raspberry_Pi_3 = Raspberry Pi 3 [part_number=RPI-3-V1.2]
  Alarme = Loudspeaker
  MPU_–_9250 = SparkFun IMU Breakout - MPU-9250

nets:
  N1: SIM868.RXI, Raspberry_Pi_3.GPIO14
  N2: SIM868.TXO, Raspberry_Pi_3.GPIO15
  N3: SIM868.POWER, Raspberry_Pi_3.5V
  GND: SIM868.GND, Raspberry_Pi_3.GND, Alarme.pin2, MPU_–_9250.GND
  3V3: Raspberry_Pi_3.3v3, MPU_–_9250.VDD
  N4: Raspberry_Pi_3.GPIO2, MPU_–_9250.SDA/SDI
  N5: Raspberry_Pi_3.GPIO3, MPU_–_9250.SCL/SCLK
  N6: Raspberry_Pi_3.GPIO17, Alarme.pin1
